// Digital circuit ALU.dig as structural Verilog
module ALU (
  input  [15:0] A,
  input  [15:0] B,
  input  [4:0] OP,
  input  C_en,
  input  C_in,
  output [15:0] R,
  output R_N,
  output R_C,
  output R_V,
  output R_Z
);

  wire and_3_out, and_4_out, and_5_out, and_6_out, and_7_out, not_2_out;
  wire [4:0] lea_shwhich_out;
  wire [15:0] add_1_s, and_2_out, idiv_q, idiv_r, inc_dec_s, lea_adder_s, lea_mul_out, lsh_rol_out,
       multiplexer_1_out, multiplexer_2_out, multiplexer_3_out, multiplexer_4_out, multiplexer_5_out,
       not_1_out, or_1_out, or_2_out, or_3_out, rsh_ror_out, sub_1_s, udiv_q, udiv_r, xor_1_out;
  wire [15:15] and_1_out;
  wire [31:0] imul_mul, umul_mul;

  and and_1 (and_1_out[15], C_en, C_in);
  LookUpTable #(.Bits(5)) lea_shwhich (.in0(OP[0]), .in1(OP[1]), .in2(OP[2]), .in3(OP[3]), .out(lea_shwhich_out));
  Multiplexer #(.Bits(16)) multiplexer_1 (.sel(C_en), .in_0(16'h1), .in_1({16{1'b1}}), .out(multiplexer_1_out));
  Add #(.Bits(16)) add_1 (.a(A), .b(B), .c_i(and_1_out[15]), .s(add_1_s));  // open: c_o
  Sub #(.Bits(16)) sub_1 (.a(A), .b(B), .c_i(and_1_out[15]), .s(sub_1_s));  // open: c_o
  BarrelShifter #(.Bits(16)) lsh_rol (.in(A), .shift(B[4:0]), .out(lsh_rol_out));
  BarrelShifter #(.Bits(16), .direction("right")) rsh_ror (.in(A), .shift(B[4:0]), .out(rsh_ror_out));
  assign not_1_out = ~A;  // Not not_1, 16 bits wide
  assign or_1_out = A | B;  // Or or_1, 16 bits wide
  assign xor_1_out = A ^ B;  // XOr xor_1, 16 bits wide
  assign and_2_out = A & B;  // And and_2, 16 bits wide
  BarrelShifter #(.Bits(16)) lea_mul (.in(B), .shift(lea_shwhich_out), .out(lea_mul_out));
  Div #(.Bits(16)) udiv (.a(A), .b(B), .q(udiv_q), .r(udiv_r));
  Div #(.Signed("true"), .Bits(16)) idiv (.a(A), .b(B), .q(idiv_q), .r(idiv_r));
  Add #(.Bits(16)) inc_dec (.a(A), .b(multiplexer_1_out), .c_i(1'b0), .s(inc_dec_s));  // open: c_o
  Mul #(.Bits(16)) umul (.a(A), .b(B), .mul(umul_mul));
  Mul #(.Signed("true"), .Bits(16)) imul (.a(A), .b(B), .mul(imul_mul));
  Multiplexer #(.Bits(16)) multiplexer_2 (.sel(OP[4]), .in_0(udiv_q), .in_1(udiv_r), .out(multiplexer_2_out));
  Multiplexer #(.Bits(16)) multiplexer_3 (.sel(OP[4]), .in_0(idiv_q), .in_1(idiv_r), .out(multiplexer_3_out));
  Multiplexer #(.Bits(16)) multiplexer_4 (
    .sel(C_en), .in_0(umul_mul[15:0]), .in_1(imul_mul[15:0]), .out(multiplexer_4_out));
  assign or_2_out = {{15{1'b0}}, and_1_out[15]} | lsh_rol_out;  // Or or_2, 16 bits wide
  Add #(.Bits(16)) lea_adder (.a(A), .b(lea_mul_out), .c_i(1'b0), .s(lea_adder_s));  // open: c_o
  Multiplexer #(.Bits(16)) multiplexer_5 (
    .sel(C_en), .in_0(multiplexer_2_out), .in_1(multiplexer_3_out), .out(multiplexer_5_out));
  assign or_3_out = {and_1_out[15], {15{1'b0}}} | rsh_ror_out;  // Or or_3, 16 bits wide
  Multiplexer #(.Selector_Bits(4), .Bits(16)) multiplexer_6 (
    .sel(OP[3:0]), .in_0(B), .in_1(add_1_s), .in_2(sub_1_s), .in_3(multiplexer_4_out), .in_4(or_2_out),
    .in_5(or_3_out), .in_6(not_1_out), .in_7(or_1_out), .in_8(xor_1_out), .in_9(and_2_out),
    .in_10(lea_adder_s), .in_11(lea_adder_s), .in_12(lea_adder_s), .in_13(multiplexer_5_out),
    .in_14(inc_dec_s), .in_15(sub_1_s), .out(R));
  and and_3 (and_3_out, A[15], B[15]);
  and and_4 (and_4_out, ~A[15], ~B[15], ~not_2_out);  // And
  and and_5 (and_5_out, not_2_out, B[15], A[15]);
  and and_6 (and_6_out, A[15], not_2_out);
  and and_7 (and_7_out, B[15], not_2_out);
  not not_2 (not_2_out, R[15]);
  or or_4 (R_V, and_4_out, and_5_out);
  or or_5 (R_C, and_6_out, and_3_out, and_7_out);
  Comparator #(.Bits(16)) comparator_1 (.a(R), .b({16{1'b0}}), .eq(R_Z));  // open: gt, lt

  assign R_N = R[15];

  // Notes on the sheet:
  //   contents of lea_shwhich (hex, n*v repeats v):
  //   10*0,1,2,3
endmodule
