// Digital circuit IOMEM.dig as structural Verilog
module IOMEM (
  input  [4:0] WADDR,
  input  [15:0] WVALUE,
  input  [15:0] FLAGSIN,
  input  W_EN,
  input  FLAGSW_EN,
  input  CLK,
  input  [4:0] RADDR,
  input  SPW_EN,
  input  [15:0] SPIN,
  input  [15:0] PINA,
  input  [15:0] PINB,
  input  [15:0] TRX,
  input  [15:0] INTNO,
  input  [15:0] IRETA,
  input  INT_EN,
  output [15:0] SP,
  output [15:0] FLAGS,
  output [15:0] RVALUE,
  output [15:0] PORTA,
  output [15:0] PORTB,
  output [15:0] TTX,
  output [15:0] PULSE,
  output [15:0] GIMSK
);

  wire decoder_1_out_1, decoder_1_out_2, decoder_1_out_3, decoder_1_out_4, decoder_1_out_7, decoder_1_out_9,
       decoder_1_out_10, decoder_1_out_11, decoder_1_out_12, decoder_1_out_13, decoder_1_out_14,
       decoder_1_out_15, decoder_1_out_17, decoder_1_out_18, decoder_1_out_19, decoder_1_out_20,
       decoder_1_out_21, decoder_1_out_22, decoder_1_out_23, decoder_1_out_24, decoder_1_out_25,
       decoder_1_out_26, decoder_1_out_27, decoder_1_out_28, decoder_1_out_29, or_1_out, or_2_out;
  wire [4:0] driver_1_out;
  wire [15:0] INTNO_q, IRETA_q, multiplexer_1_out, multiplexer_2_out, multiplexer_3_out, PCAMSK_q, PCBMSK_q,
       PINA_q, PINB_q, TODO_2_q, TODO_3_q, TODO_4_q, TODO_5_q, TODO_6_q, TODO_7_q, TODO_8_q, TODO_9_q,
       TODO_10_q, TODO_11_q, TODO_12_q, TODO_13_q, TODO_14_q, TODO_15_q, TODO_16_q, TODO_17_q, TODO_q, TRX_q;

  Multiplexer #(.Bits(16)) multiplexer_1 (.sel(SPW_EN), .in_0(WVALUE), .in_1(SPIN), .out(multiplexer_1_out));
  or or_1 (or_1_out, SPW_EN, decoder_1_out_1);
  assign driver_1_out = W_EN ? WADDR : 5'bz;  // Driver driver_1
  assign driver_1_out = ~W_EN ? {5{1'b0}} : 5'bz;  // DriverInvSel driverinvsel_1
  Decoder #(.Selector_Bits(5)) decoder_1 (
    .sel(driver_1_out), .out_1(decoder_1_out_1), .out_2(decoder_1_out_2), .out_3(decoder_1_out_3),
    .out_4(decoder_1_out_4), .out_7(decoder_1_out_7), .out_9(decoder_1_out_9), .out_10(decoder_1_out_10),
    .out_11(decoder_1_out_11), .out_12(decoder_1_out_12), .out_13(decoder_1_out_13),
    .out_14(decoder_1_out_14), .out_15(decoder_1_out_15), .out_16(decoder_1_out_15),
    .out_17(decoder_1_out_17), .out_18(decoder_1_out_18), .out_19(decoder_1_out_19),
    .out_20(decoder_1_out_20), .out_21(decoder_1_out_21), .out_22(decoder_1_out_22),
    .out_23(decoder_1_out_23), .out_24(decoder_1_out_24), .out_25(decoder_1_out_25),
    .out_26(decoder_1_out_26), .out_27(decoder_1_out_27), .out_28(decoder_1_out_28), .out_29(decoder_1_out_29));  // open: out_0, out_5, out_6, out_8, out_30, out_31
  Register #(.Bits(16)) u_SP (.D(multiplexer_1_out), .C(CLK), .en(or_1_out), .Q(SP));
  or or_2 (or_2_out, FLAGSW_EN, decoder_1_out_2);
  Multiplexer #(.Bits(16)) multiplexer_2 (.sel(FLAGSW_EN), .in_0(WVALUE), .in_1(FLAGSIN), .out(multiplexer_2_out));
  Register #(.Bits(16)) u_FLAGS (.D(multiplexer_2_out), .C(CLK), .en(or_2_out), .Q(FLAGS));
  Register #(.Bits(16)) u_PORTA (.D(WVALUE), .C(CLK), .en(decoder_1_out_3), .Q(PORTA));
  Register #(.Bits(16)) u_PORTB (.D(WVALUE), .C(CLK), .en(decoder_1_out_4), .Q(PORTB));
  Register #(.Bits(16)) u_PINA (.D(PINA), .C(CLK), .en(1'b1), .Q(PINA_q));
  Register #(.Bits(16)) u_PINB (.D(PINB), .C(CLK), .en(1'b1), .Q(PINB_q));
  Register #(.Bits(16)) u_TTX (.D(WVALUE), .C(CLK), .en(decoder_1_out_7), .Q(TTX));
  Register #(.Bits(16)) u_TRX (.D(TRX), .C(CLK), .en(1'b1), .Q(TRX_q));
  Register #(.Bits(16)) u_PULSE (.D(multiplexer_3_out), .C(CLK), .en(1'b1), .Q(PULSE));
  Multiplexer #(.Bits(16)) multiplexer_3 (
    .sel(decoder_1_out_9), .in_0({16{1'b0}}), .in_1(WVALUE), .out(multiplexer_3_out));
  Register #(.Bits(16)) TODO (.D(WVALUE), .C(CLK), .en(decoder_1_out_10), .Q(TODO_q));
  Register #(.Bits(16)) TODO_2 (.D(WVALUE), .C(CLK), .en(decoder_1_out_11), .Q(TODO_2_q));
  Register #(.Bits(16)) TODO_3 (.D(WVALUE), .C(CLK), .en(decoder_1_out_12), .Q(TODO_3_q));
  Register #(.Bits(16)) TODO_4 (.D(WVALUE), .C(CLK), .en(decoder_1_out_13), .Q(TODO_4_q));
  Register #(.Bits(16)) TODO_5 (.D(WVALUE), .C(CLK), .en(decoder_1_out_14), .Q(TODO_5_q));
  Register #(.Bits(16)) TODO_6 (.D(WVALUE), .C(CLK), .en(decoder_1_out_15), .Q(TODO_6_q));
  Register #(.Bits(16)) TODO_7 (.D(WVALUE), .C(CLK), .en(decoder_1_out_15), .Q(TODO_7_q));
  Register #(.Bits(16)) TODO_8 (.D(WVALUE), .C(CLK), .en(decoder_1_out_17), .Q(TODO_8_q));
  Register #(.Bits(16)) TODO_9 (.D(WVALUE), .C(CLK), .en(decoder_1_out_18), .Q(TODO_9_q));
  Register #(.Bits(16)) TODO_10 (.D(WVALUE), .C(CLK), .en(decoder_1_out_19), .Q(TODO_10_q));
  Register #(.Bits(16)) TODO_11 (.D(WVALUE), .C(CLK), .en(decoder_1_out_20), .Q(TODO_11_q));
  Register #(.Bits(16)) TODO_12 (.D(WVALUE), .C(CLK), .en(decoder_1_out_21), .Q(TODO_12_q));
  Register #(.Bits(16)) TODO_13 (.D(WVALUE), .C(CLK), .en(decoder_1_out_22), .Q(TODO_13_q));
  Register #(.Bits(16)) TODO_14 (.D(WVALUE), .C(CLK), .en(decoder_1_out_23), .Q(TODO_14_q));
  Register #(.Bits(16)) TODO_15 (.D(WVALUE), .C(CLK), .en(decoder_1_out_24), .Q(TODO_15_q));
  Register #(.Bits(16)) TODO_16 (.D(WVALUE), .C(CLK), .en(decoder_1_out_25), .Q(TODO_16_q));
  Register #(.Bits(16)) TODO_17 (.D(WVALUE), .C(CLK), .en(decoder_1_out_26), .Q(TODO_17_q));
  Register #(.Bits(16)) PCAMSK (.D(WVALUE), .C(CLK), .en(decoder_1_out_27), .Q(PCAMSK_q));
  Register #(.Bits(16)) PCBMSK (.D(WVALUE), .C(CLK), .en(decoder_1_out_28), .Q(PCBMSK_q));
  Register #(.Bits(16)) u_GIMSK (.D(WVALUE), .C(CLK), .en(decoder_1_out_29), .Q(GIMSK));
  Register #(.Bits(16)) u_IRETA (.D(IRETA), .C(CLK), .en(INT_EN), .Q(IRETA_q));
  Register #(.Bits(16)) u_INTNO (.D(INTNO), .C(CLK), .en(INT_EN), .Q(INTNO_q));
  Multiplexer #(.Selector_Bits(5), .Bits(16)) multiplexer_4 (
    .sel(RADDR), .in_0({16{1'b0}}), .in_1(SP), .in_2(FLAGS), .in_3(PORTA), .in_4(PORTB), .in_5(PINA_q),
    .in_6(PINB_q), .in_7(TTX), .in_8(TRX_q), .in_9(PULSE), .in_10(TODO_q), .in_11(TODO_2_q),
    .in_12(TODO_3_q), .in_13(TODO_4_q), .in_14(TODO_5_q), .in_15(TODO_6_q), .in_16(TODO_7_q),
    .in_17(TODO_8_q), .in_18(TODO_9_q), .in_19(TODO_10_q), .in_20(TODO_11_q), .in_21(TODO_12_q),
    .in_22(TODO_13_q), .in_23(TODO_14_q), .in_24(TODO_15_q), .in_25(TODO_16_q), .in_26(TODO_17_q),
    .in_27(PCAMSK_q), .in_28(PCBMSK_q), .in_29(GIMSK), .in_30(IRETA_q), .in_31(INTNO_q), .out(RVALUE));
endmodule
